# Fritzing sketch Schematic (saved by Fritzing 0.9.6b)
breadboards: 1

parts:
  Part1 = Arduino Mega 2560 (Rev3)
  ZS-042_RTC1 = ZS-042 RTC Module
  LED1 = smd LED [color="Infrared (850nm)" package="0603 [SMD]"]  # not connected

nets:
  N1: Part1.D21/SCL, ZS-042_RTC1.SCL
  N2: Part1.D20/SDA, ZS-042_RTC1.SDA
  3V3: Part1.3V3, ZS-042_RTC1.VCC
  GND: Part1.GND, ZS-042_RTC1.GND
